# Fritzing sketch UnoPico0207 (saved by Fritzing 0.9.4)
breadboards: 1

parts:
  元件1 = UnoPico Fritz Part
  元件2 = NeoPixel Stick [part_number=1426]
  LCD1 = TFT 1.8 inch 160x128 w SD

nets:
  N1: 元件1.TX0, 元件2.DATAIN
  N2: 元件1.VCC, LCD1.pin_1, LCD1.pin_8
  GND: 元件1.GND, 元件2.GND, LCD1.pin2
  N3: 元件1.NSS, LCD1.pin3
  N4: 元件1.RST, LCD1.pin4
  N5: 元件1.NA7_LCD_CD, LCD1.pin_5
  N6: 元件1.NMOSI, LCD1.pin_6
  N7: 元件1.NSCK, LCD1.pin_7
  5V: 元件1.5V, 元件2.+5V

custom parts:
  UnoPico Fritz Part: UnoPicoNanoQ
  NeoPixel Stick: Make your own little LED strip arrangement with this stick of NeoPixel LEDs. We crammed 8 of the tiny 5050 (5mm x 5mm) smart RGB LEDs onto a PCB with mounting holes and a chainable design. Use only one microcontroller pin to control as many as you can chain together! Each LED is addressable as the driver chip is inside the LED. Each one has ~18mA constant current drive so the color will be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
  TFT 1.8 inch 160x128 w SD: This is a generic 1.8 tft spi lcd display available on ebay and others. The 1.8" display has 128x160 color pixels and in this version pin names in breadboard (unlike the real board).
